# Fritzing sketch Design (saved by Fritzing 0.9.3b)
circuit board: 8.83926cm x 5.3226cm

parts:
  U1 = LCD-16X2 [package=lcd-16x2_nosilk]
  R2 = Trimmer Potentiometer [maximum_resistance=10kΩ package=THT]
  R3 = Resistor [tolerance=±5% resistance=220 package="2512 [SMD]"]
  Arduino1 = Arduino Mini (Rev5)
  Part2 = MicroSD Card Module
  DS1 = DS18B20 1-Wire Temperature Sensor [part_number=DS18B20]
  ZS-042_RTC1 = ZS-042 RTC Module
  R1 = Resistor [tolerance=±5% resistance=220 package="2512 [SMD]"]

nets:
  GND: U1.VSS, U1.R_W, U1.K, R2.leg2, Arduino1.GND, Part2.GND, DS1.GND, ZS-042_RTC1.GND
  VDD: U1.VDD, R2.leg1, R3.Pin_1, Arduino1.5V, Part2.VCC, DS1.VDD, ZS-042_RTC1.VCC, R1.Pin_0
  N1: U1.VO, R2.wiper
  N2: U1.RS, Arduino1.D9_PWM
  N3: U1.E, Arduino1.D8
  N4: U1.DB4, Arduino1.D5_PWM
  N5: U1.DB5, Arduino1.D4
  N6: U1.DB6, Arduino1.D3_PWM
  N7: U1.DB7, Arduino1.D2
  N8: U1.A, R3.Pin_0
  N9: Arduino1.D6_PWM, DS1.DQ, R1.Pin_1
  N10: Arduino1.D7, Part2.CS
  N11: Arduino1.D12, Part2.SCK
  N12: Arduino1.D11_PWM, Part2.MISO
  N13: Arduino1.D10_PWM, Part2.MOSI
  N14: Arduino1.A4, ZS-042_RTC1.SDA
  N15: Arduino1.A5, ZS-042_RTC1.SCL
